// Logisim project automatic_cs.circ as structural Verilog: 14 circuits, main circuit main
module main (
  input  in_1,
  input  in_2,
  input  in_3,
  input  [7:0] in_4,
  input  in_5,
  input  in_6,
  input  in_7,
  input  in_8,
  input  in_9,
  input  in_10,
  input  in_11,
  input  [7:0] in_12,
  input  in_13,
  input  in_14,
  input  in_15,
  input  in_16,
  input  in_17,
  input  in_18,
  input  in_19,
  output [3:0] out_20,
  output [7:0] out_21,
  output [7:0] out_22,
  output [7:0] out_23,
  output [7:0] out_24,
  output [7:0] out_25,
  output [7:0] out_26,
  output [7:0] out_27,
  output [7:0] out_28,
  output [7:0] out_29,
  output [7:0] out_30,
  output [7:0] out_31,
  output [7:0] out_32,
  output [7:0] out_33,
  output [7:0] out_34,
  output [7:0] out_35,
  output [7:0] out_36,
  output [7:0] out_37,
  output [7:0] out_38,
  output [7:0] out_39,
  output [7:0] out_40,
  output [7:0] out_41,
  output [3:0] out_42,
  output [3:0] out_43,
  output [3:0] out_44,
  output [7:0] out_45,
  output [7:0] out_46,
  output [7:0] out_47,
  output [7:0] out_48,
  output [7:0] out_49,
  output [3:0] out_50
);

  wire a_in, a_out, alu_out, alu_sub, b_in, b_out, hlt, i1, i2, ins_reg_in_en, ins_reg_out_en, jump_en,
       mar_in_en, pc_en, pc_out, sh_dir, sh_out, sh_rot, sram_rd, sram_wr;
  wire [3:0] multiplexer_1_out, multiplexer_1_out_2;
  wire [7:0] debug_data, reg_gp_3_reg_int_out, reg_gp_4_reg_int_out, shifter_1_out, shifter_2_out,
       shifter_3_out, shifter_4_out;
  wire [7:4] undriven;

  Hex_Digit_Display hex_digit_display_1 (.value(multiplexer_1_out_2));  // open: dp
  Hex_Digit_Display hex_digit_display_2 (.value(multiplexer_1_out));  // open: dp
  Multiplexer #(.width(8)) multiplexer_1 (
    .in0(out_21), .in1({undriven, out_44}), .out({multiplexer_1_out_2, multiplexer_1_out}), .sel(in_1));
  pc_loader pc_loader_1 (
    .pc_reset(in_2), .load_or_count(jump_en), .pc_en(pc_en), .clk(in_3), .data_load(out_21[3:0]),
    .pc_out_en(pc_out), .pc_value(out_20), .pc_out(out_21[3:0]));
  sram sram_1 (
    .sram_rd(sram_rd), .sram_wr(sram_wr), .sram_d_in(out_21),
    .mar_d_in({multiplexer_1_out_2, multiplexer_1_out}), .mar_in_en(mar_in_en), .sram_clk(in_3),
    .sram_d_out(out_21), .out_8(out_23), .out_9(out_24), .out_10(out_25), .out_11(out_26), .out_12(out_27),
    .out_13(out_28), .out_14(out_30), .out_15(out_31), .out_16(out_32), .out_17(out_34), .out_18(out_35),
    .out_19(out_37), .out_20(out_38), .out_21(out_39), .out_22(out_40), .out_23(out_41));
  Hex_Digit_Display hex_digit_display_3 (.value(out_20));  // open: dp
  ins_loader ins_loader_1 (.bc_reset(in_2), .bc_en(i2), .clk(in_3), .debug(in_1), .out_5(out_44), .i1(i1), .i2(i2));
  Hex_Digit_Display hex_digit_display_4 (.value(out_21[7:4]));  // open: dp
  Hex_Digit_Display hex_digit_display_5 (.value(out_44));  // open: dp
  Hex_Digit_Display hex_digit_display_6 (.value(out_21[3:0]));  // open: dp
  ROM #(.addrWidth(4)) rom_1 (.addr(out_44), .data(debug_data));
  assign out_21 = in_1 ? debug_data : 8'bz;  // Controlled_Buffer controlled_buffer_1
  reg_gp reg_gp_1 (
    .reg_in(out_21), .reg_in_en(a_in), .reg_clk(in_3), .reg_out_in(a_out), .reg_int_out(out_22),
    .reg_out(out_21));
  reg_gp reg_gp_2 (
    .reg_in(out_21), .reg_in_en(b_in), .reg_clk(in_3), .reg_out_in(b_out), .reg_int_out(out_36),
    .reg_out(out_21));
  ins_reg ins_reg_1 (
    .ins_reg_in(out_21), .ins_reg_in_en(ins_reg_in_en), .clk(in_3), .ins_reg_out_en(ins_reg_out_en),
    .add_outs(out_21[3:0]), .ins_out(out_43));
  Hex_Digit_Display hex_digit_display_7 (.value(out_36[7:4]));  // open: dp
  Hex_Digit_Display hex_digit_display_8 (.value(out_21[3:0]));  // open: dp
  Hex_Digit_Display hex_digit_display_9 (.value(out_22[7:4]));  // open: dp
  Hex_Digit_Display hex_digit_display_10 (.value(out_36[3:0]));  // open: dp
  Hex_Digit_Display hex_digit_display_11 (.value(out_43));  // open: dp
  Hex_Digit_Display hex_digit_display_12 (.value(out_22[3:0]));  // open: dp
  alu alu_1 (
    .alu_in_1(out_22), .alu_out_en(alu_out), .alu_sub(alu_sub), .alu_in_2(out_36), .alu_out(out_21));  // open: alu_carry_out
  LED led_1 (.in(in_1));
  Shifter shifter_1 (.in(out_22), .\dist (3'b001), .out(shifter_1_out));
  Shifter #(.shift("lr")) shifter_2 (.in(out_22), .\dist (3'b001), .out(shifter_2_out));
  cs cs_1 (
    .clk(in_3), .clk_reset(in_2), .ins_msb(out_43), .i1(i1), .debug(in_1), .i2(i2), .sh_dir(sh_dir),
    .sh_out(sh_out), .sh_rot(sh_rot), .ins_reg_in_en(ins_reg_in_en), .a_in(a_in), .a_out(a_out), .b_in(b_in),
    .alu_out(alu_out), .sram_wr(sram_wr), .hlt(hlt), .sub_out(alu_sub), .jump_en(jump_en),
    .ins_reg_out_en(ins_reg_out_en), .mar_in_en(mar_in_en), .sram_rd(sram_rd), .pc_out(pc_out), .pc_en(pc_en));
  Shifter #(.shift("rl")) shifter_3 (.in(out_22), .\dist (3'b001), .out(shifter_3_out));
  Multiplexer #(.select(2), .width(8)) multiplexer_2 (
    .in0(shifter_1_out), .in1(shifter_2_out), .in2(shifter_3_out), .in3(shifter_4_out), .out(out_29),
    .sel({sh_rot, sh_dir}));
  Shifter #(.shift("rr")) shifter_4 (.in(out_22), .\dist (3'b001), .out(shifter_4_out));
  assign out_21 = sh_out ? out_29 : 8'bz;  // Controlled_Buffer controlled_buffer_2
  reg_gp reg_gp_3 (
    .reg_in(in_4), .reg_in_en(in_5), .reg_clk(in_6), .reg_out_in(in_7), .reg_int_out(reg_gp_3_reg_int_out),
    .reg_out(out_45));
  reg_gp reg_gp_4 (
    .reg_in(in_4), .reg_in_en(in_10), .reg_clk(in_6), .reg_out_in(in_11), .reg_int_out(reg_gp_4_reg_int_out),
    .reg_out(out_47));
  alu alu_2 (
    .alu_in_1(reg_gp_3_reg_int_out), .alu_out_en(in_8), .alu_sub(in_9), .alu_in_2(reg_gp_4_reg_int_out),
    .alu_out(out_46));  // open: alu_carry_out
  pc pc_1 (.pc_en(in_16), .pc_clk(in_17), .pc_reset(in_18), .pc_out_en(in_19), .pc_value(out_50));  // open: pc_out
  reg_gp reg_gp_5 (
    .reg_in(in_12), .reg_in_en(in_13), .reg_clk(in_14), .reg_out_in(in_15), .reg_int_out(out_48),
    .reg_out(out_49));

  assign out_33 = out_21;
  assign out_42 = out_21[3:0];

  // Other names for the same wires on the sheet: bc_address[3:0] = out_44; clk = in_3; debug = in_1;
  //   ir_operand[3:0] = out_21[3:0]; pc_reset = in_2

  // Notes on the sheet:
  //   MAR Value
  //   Counter Value
  //   Data Bus
  //   contents of rom_1 (hex, n*v repeats v):
  //   1c 70 5f 1c 80 5e 1c 90 5d 1c a0 5b 19
  //   Loader Counter Value
  //   Ins_operand
  //   Register A
  //   Ins_opcode
  //   Register B
endmodule

module reg_gp (
  input  [7:0] reg_in,
  input  reg_in_en,
  input  reg_clk,
  input  reg_out_in,
  output [7:0] reg_int_out,
  output [7:0] reg_out
);

  wire multiplexer_1_out, multiplexer_2_out, multiplexer_3_out, multiplexer_4_out, multiplexer_5_out,
       multiplexer_6_out, multiplexer_7_out, multiplexer_8_out;

  Multiplexer multiplexer_1 (.in0(reg_int_out[7]), .in1(reg_in[7]), .out(multiplexer_1_out), .sel(reg_in_en));
  D_Flip_Flop d_ff_1 (.D(multiplexer_1_out), .clk(reg_clk), .Q(reg_int_out[7]));  // open: Qn, preset, reset
  assign reg_out[7] = reg_out_in ? reg_int_out[7] : 1'bz;  // Controlled_Buffer controlled_buffer_1
  Multiplexer multiplexer_2 (.in0(reg_int_out[6]), .in1(reg_in[6]), .out(multiplexer_2_out), .sel(reg_in_en));
  D_Flip_Flop d_ff_2 (.D(multiplexer_2_out), .clk(reg_clk), .Q(reg_int_out[6]));  // open: Qn, preset, reset
  assign reg_out[6] = reg_out_in ? reg_int_out[6] : 1'bz;  // Controlled_Buffer controlled_buffer_2
  Multiplexer multiplexer_3 (.in0(reg_int_out[5]), .in1(reg_in[5]), .out(multiplexer_3_out), .sel(reg_in_en));
  D_Flip_Flop d_ff_3 (.D(multiplexer_3_out), .clk(reg_clk), .Q(reg_int_out[5]));  // open: Qn, preset, reset
  assign reg_out[5] = reg_out_in ? reg_int_out[5] : 1'bz;  // Controlled_Buffer controlled_buffer_3
  Multiplexer multiplexer_4 (.in0(reg_int_out[4]), .in1(reg_in[4]), .out(multiplexer_4_out), .sel(reg_in_en));
  D_Flip_Flop d_ff_4 (.D(multiplexer_4_out), .clk(reg_clk), .Q(reg_int_out[4]));  // open: Qn, preset, reset
  assign reg_out[4] = reg_out_in ? reg_int_out[4] : 1'bz;  // Controlled_Buffer controlled_buffer_4
  Multiplexer multiplexer_5 (.in0(reg_int_out[3]), .in1(reg_in[3]), .out(multiplexer_5_out), .sel(reg_in_en));
  D_Flip_Flop d_ff_5 (.D(multiplexer_5_out), .clk(reg_clk), .Q(reg_int_out[3]));  // open: Qn, preset, reset
  Multiplexer multiplexer_6 (.in0(reg_int_out[2]), .in1(reg_in[2]), .out(multiplexer_6_out), .sel(reg_in_en));
  D_Flip_Flop d_ff_6 (.D(multiplexer_6_out), .clk(reg_clk), .Q(reg_int_out[2]));  // open: Qn, preset, reset
  assign reg_out[3] = reg_out_in ? reg_int_out[3] : 1'bz;  // Controlled_Buffer controlled_buffer_5
  assign reg_out[2] = reg_out_in ? reg_int_out[2] : 1'bz;  // Controlled_Buffer controlled_buffer_6
  Multiplexer multiplexer_7 (.in0(reg_int_out[1]), .in1(reg_in[1]), .out(multiplexer_7_out), .sel(reg_in_en));
  D_Flip_Flop d_ff_7 (.D(multiplexer_7_out), .clk(reg_clk), .Q(reg_int_out[1]));  // open: Qn, preset, reset
  assign reg_out[1] = reg_out_in ? reg_int_out[1] : 1'bz;  // Controlled_Buffer controlled_buffer_7
  Multiplexer multiplexer_8 (.in0(reg_int_out[0]), .in1(reg_in[0]), .out(multiplexer_8_out), .sel(reg_in_en));
  D_Flip_Flop d_ff_8 (.D(multiplexer_8_out), .clk(reg_clk), .Q(reg_int_out[0]));  // open: Qn, preset, reset
  assign reg_out[0] = reg_out_in ? reg_int_out[0] : 1'bz;  // Controlled_Buffer controlled_buffer_8
endmodule

module alu (
  input  [7:0] alu_in_1,
  input  alu_out_en,
  input  alu_sub,
  input  [7:0] alu_in_2,
  output alu_carry_out,
  output [7:0] alu_out
);

  wire adder_2_cout, adder_3_cout, adder_4_cout, adder_5_cout, adder_6_cout, adder_7_cout, adder_8_cout,
       xor_1_out, xor_2_out, xor_3_out, xor_4_out, xor_5_out, xor_6_out, xor_7_out, xor_8_out;
  wire [7:0] adder_8_out;

  Adder #(.width(1)) adder_1 (
    .a(alu_in_1[7]), .b(xor_1_out), .out(adder_8_out[7]), .cin(adder_2_cout), .cout(alu_carry_out));
  xor xor_1 (xor_1_out, alu_in_2[7], alu_sub);
  Adder #(.width(1)) adder_2 (
    .a(alu_in_1[6]), .b(xor_2_out), .out(adder_8_out[6]), .cin(adder_3_cout), .cout(adder_2_cout));
  xor xor_2 (xor_2_out, alu_in_2[6], alu_sub);
  Adder #(.width(1)) adder_3 (
    .a(alu_in_1[5]), .b(xor_3_out), .out(adder_8_out[5]), .cin(adder_4_cout), .cout(adder_3_cout));
  xor xor_3 (xor_3_out, alu_in_2[5], alu_sub);
  Adder #(.width(1)) adder_4 (
    .a(alu_in_1[4]), .b(xor_4_out), .out(adder_8_out[4]), .cin(adder_5_cout), .cout(adder_4_cout));
  xor xor_4 (xor_4_out, alu_in_2[4], alu_sub);
  Adder #(.width(1)) adder_5 (
    .a(alu_in_1[3]), .b(xor_5_out), .out(adder_8_out[3]), .cin(adder_6_cout), .cout(adder_5_cout));
  xor xor_5 (xor_5_out, alu_in_2[3], alu_sub);
  Adder #(.width(1)) adder_6 (
    .a(alu_in_1[2]), .b(xor_6_out), .out(adder_8_out[2]), .cin(adder_7_cout), .cout(adder_6_cout));
  xor xor_6 (xor_6_out, alu_in_2[2], alu_sub);
  Adder #(.width(1)) adder_7 (
    .a(alu_in_1[1]), .b(xor_7_out), .out(adder_8_out[1]), .cin(adder_8_cout), .cout(adder_7_cout));
  xor xor_7 (xor_7_out, alu_in_2[1], alu_sub);
  Adder #(.width(1)) adder_8 (.a(alu_in_1[0]), .b(xor_8_out), .out(adder_8_out[0]), .cin(alu_sub), .cout(adder_8_cout));
  xor xor_8 (xor_8_out, alu_in_2[0], alu_sub);
  assign alu_out = alu_out_en ? adder_8_out : 8'bz;  // Controlled_Buffer controlled_buffer_1
endmodule

module pc (
  input  pc_en,
  input  pc_clk,
  input  pc_reset,
  input  pc_out_en,
  output [3:0] pc_value,
  output [3:0] pc_out
);

  wire j_k_ff_2_qn, j_k_ff_3_qn, j_k_ff_4_qn;

  J_K_Flip_Flop j_k_ff_1 (
    .J(pc_en), .K(pc_en), .clk(j_k_ff_2_qn), .Q(pc_value[3]), .reset(pc_reset));  // open: Qn, preset
  J_K_Flip_Flop j_k_ff_2 (
    .J(pc_en), .K(pc_en), .clk(j_k_ff_3_qn), .Q(pc_value[2]), .Qn(j_k_ff_2_qn), .reset(pc_reset));  // open: preset
  J_K_Flip_Flop j_k_ff_3 (
    .J(pc_en), .K(pc_en), .clk(j_k_ff_4_qn), .Q(pc_value[1]), .Qn(j_k_ff_3_qn), .reset(pc_reset));  // open: preset
  J_K_Flip_Flop j_k_ff_4 (
    .J(pc_en), .K(pc_en), .clk(pc_clk), .Q(pc_value[0]), .Qn(j_k_ff_4_qn), .reset(pc_reset));  // open: preset
  assign pc_out = pc_out_en ? pc_value : 4'bz;  // Controlled_Buffer controlled_buffer_1
endmodule

module dec_4x16 (
  input  [3:0] dec_sel,
  output [15:0] dec_out
);

  wire not_1_out, not_2_out, not_3_out, not_4_out;

  not not_1 (not_1_out, dec_sel[3]);
  not not_2 (not_2_out, dec_sel[2]);
  not not_3 (not_3_out, dec_sel[1]);
  not not_4 (not_4_out, dec_sel[0]);
  and and_1 (dec_out[0], not_4_out, not_3_out, not_2_out, not_1_out);
  and and_2 (dec_out[1], dec_sel[0], not_3_out, not_2_out, not_1_out);
  and and_3 (dec_out[2], not_4_out, dec_sel[1], not_2_out, not_1_out);
  and and_4 (dec_out[3], dec_sel[0], dec_sel[1], not_2_out, not_1_out);
  and and_5 (dec_out[4], not_4_out, not_3_out, dec_sel[2], not_1_out);
  and and_6 (dec_out[5], dec_sel[0], not_3_out, dec_sel[2], not_1_out);
  and and_7 (dec_out[6], not_4_out, dec_sel[1], dec_sel[2], not_1_out);
  and and_8 (dec_out[7], dec_sel[0], dec_sel[1], dec_sel[2], not_1_out);
  and and_9 (dec_out[8], not_4_out, not_3_out, not_2_out, dec_sel[3]);
  and and_10 (dec_out[9], dec_sel[0], not_3_out, not_2_out, dec_sel[3]);
  and and_11 (dec_out[10], not_4_out, dec_sel[1], not_2_out, dec_sel[3]);
  and and_12 (dec_out[11], dec_sel[0], dec_sel[1], not_2_out, dec_sel[3]);
  and and_13 (dec_out[12], not_4_out, not_3_out, dec_sel[2], dec_sel[3]);
  and and_14 (dec_out[13], dec_sel[0], not_3_out, dec_sel[2], dec_sel[3]);
  and and_15 (dec_out[14], not_4_out, dec_sel[1], dec_sel[2], dec_sel[3]);
  and and_16 (dec_out[15], dec_sel[0], dec_sel[1], dec_sel[2], dec_sel[3]);
endmodule

module sram_cell (
  input  [7:0] data_in,
  input  wr_en,
  input  clk,
  input  cs,
  input  rd_en,
  output [7:0] memory_content,
  output [7:0] data_out
);

  wire and_1_out, and_2_out;

  and and_1 (and_1_out, wr_en, cs);
  and and_2 (and_2_out, cs, rd_en);
  reg_gp reg_gp_1 (
    .reg_in(data_in), .reg_in_en(and_1_out), .reg_clk(clk), .reg_out_in(and_2_out),
    .reg_int_out(memory_content), .reg_out(data_out));
endmodule

module sram (
  input  sram_rd,
  input  sram_wr,
  input  [7:0] sram_d_in,
  input  [7:0] mar_d_in,
  input  mar_in_en,
  input  sram_clk,
  output [7:0] sram_d_out,
  output [7:0] out_8,
  output [7:0] out_9,
  output [7:0] out_10,
  output [7:0] out_11,
  output [7:0] out_12,
  output [7:0] out_13,
  output [7:0] out_14,
  output [7:0] out_15,
  output [7:0] out_16,
  output [7:0] out_17,
  output [7:0] out_18,
  output [7:0] out_19,
  output [7:0] out_20,
  output [7:0] out_21,
  output [7:0] out_22,
  output [7:0] out_23
);

  wire [7:0] controlled_buffer_1_out, reg_gp_1_reg_int_out;
  wire [15:0] dec_4x16_1_dec_out;

  reg_gp reg_gp_1 (
    .reg_in(mar_d_in), .reg_in_en(mar_in_en), .reg_clk(sram_clk), .reg_int_out(reg_gp_1_reg_int_out));  // open: reg_out_in, reg_out
  dec_4x16 dec_4x16_1 (.dec_sel(reg_gp_1_reg_int_out[3:0]), .dec_out(dec_4x16_1_dec_out));
  assign controlled_buffer_1_out = sram_wr ? sram_d_in : 8'bz;  // Controlled_Buffer controlled_buffer_1
  sram_cell sram_cell_1 (
    .data_in(controlled_buffer_1_out), .wr_en(sram_wr), .clk(sram_clk), .cs(dec_4x16_1_dec_out[0]),
    .rd_en(sram_rd), .memory_content(out_8), .data_out(controlled_buffer_1_out));
  sram_cell sram_cell_2 (
    .data_in(controlled_buffer_1_out), .wr_en(sram_wr), .clk(sram_clk), .cs(dec_4x16_1_dec_out[1]),
    .rd_en(sram_rd), .memory_content(out_9), .data_out(controlled_buffer_1_out));
  sram_cell sram_cell_3 (
    .data_in(controlled_buffer_1_out), .wr_en(sram_wr), .clk(sram_clk), .cs(dec_4x16_1_dec_out[2]),
    .rd_en(sram_rd), .memory_content(out_10), .data_out(controlled_buffer_1_out));
  sram_cell sram_cell_4 (
    .data_in(controlled_buffer_1_out), .wr_en(sram_wr), .clk(sram_clk), .cs(dec_4x16_1_dec_out[3]),
    .rd_en(sram_rd), .memory_content(out_11), .data_out(controlled_buffer_1_out));
  sram_cell sram_cell_5 (
    .data_in(controlled_buffer_1_out), .wr_en(sram_wr), .clk(sram_clk), .cs(dec_4x16_1_dec_out[4]),
    .rd_en(sram_rd), .memory_content(out_12), .data_out(controlled_buffer_1_out));
  sram_cell sram_cell_6 (
    .data_in(controlled_buffer_1_out), .wr_en(sram_wr), .clk(sram_clk), .cs(dec_4x16_1_dec_out[5]),
    .rd_en(sram_rd), .memory_content(out_13), .data_out(controlled_buffer_1_out));
  sram_cell sram_cell_7 (
    .data_in(controlled_buffer_1_out), .wr_en(sram_wr), .clk(sram_clk), .cs(dec_4x16_1_dec_out[6]),
    .rd_en(sram_rd), .memory_content(out_14), .data_out(controlled_buffer_1_out));
  sram_cell sram_cell_8 (
    .data_in(controlled_buffer_1_out), .wr_en(sram_wr), .clk(sram_clk), .cs(dec_4x16_1_dec_out[7]),
    .rd_en(sram_rd), .memory_content(out_15), .data_out(controlled_buffer_1_out));
  sram_cell sram_cell_9 (
    .data_in(controlled_buffer_1_out), .wr_en(sram_wr), .clk(sram_clk), .cs(dec_4x16_1_dec_out[8]),
    .rd_en(sram_rd), .memory_content(out_16), .data_out(controlled_buffer_1_out));
  sram_cell sram_cell_10 (
    .data_in(controlled_buffer_1_out), .wr_en(sram_wr), .clk(sram_clk), .cs(dec_4x16_1_dec_out[9]),
    .rd_en(sram_rd), .memory_content(out_17), .data_out(controlled_buffer_1_out));
  sram_cell sram_cell_11 (
    .data_in(controlled_buffer_1_out), .wr_en(sram_wr), .clk(sram_clk), .cs(dec_4x16_1_dec_out[10]),
    .rd_en(sram_rd), .memory_content(out_18), .data_out(controlled_buffer_1_out));
  sram_cell sram_cell_12 (
    .data_in(controlled_buffer_1_out), .wr_en(sram_wr), .clk(sram_clk), .cs(dec_4x16_1_dec_out[11]),
    .rd_en(sram_rd), .memory_content(out_19), .data_out(controlled_buffer_1_out));
  sram_cell sram_cell_13 (
    .data_in(controlled_buffer_1_out), .wr_en(sram_wr), .clk(sram_clk), .cs(dec_4x16_1_dec_out[12]),
    .rd_en(sram_rd), .memory_content(out_20), .data_out(controlled_buffer_1_out));
  sram_cell sram_cell_14 (
    .data_in(controlled_buffer_1_out), .wr_en(sram_wr), .clk(sram_clk), .cs(dec_4x16_1_dec_out[13]),
    .rd_en(sram_rd), .memory_content(out_21), .data_out(controlled_buffer_1_out));
  sram_cell sram_cell_15 (
    .data_in(controlled_buffer_1_out), .wr_en(sram_wr), .clk(sram_clk), .cs(dec_4x16_1_dec_out[14]),
    .rd_en(sram_rd), .memory_content(out_22), .data_out(controlled_buffer_1_out));
  sram_cell sram_cell_16 (
    .data_in(controlled_buffer_1_out), .wr_en(sram_wr), .clk(sram_clk), .cs(dec_4x16_1_dec_out[15]),
    .rd_en(sram_rd), .memory_content(out_23), .data_out(controlled_buffer_1_out));
  assign sram_d_out = sram_rd ? controlled_buffer_1_out : 8'bz;  // Controlled_Buffer controlled_buffer_2
endmodule

module ins_reg (
  input  [7:0] ins_reg_in,
  input  ins_reg_in_en,
  input  clk,
  input  ins_reg_out_en,
  output [3:0] add_outs,
  output [3:0] ins_out
);

  wire [3:0] reg_gp_1_reg_int_out;

  reg_gp reg_gp_1 (
    .reg_in(ins_reg_in), .reg_in_en(ins_reg_in_en), .reg_clk(clk),
    .reg_int_out({ins_out, reg_gp_1_reg_int_out}));  // open: reg_out_in, reg_out
  assign add_outs = ins_reg_out_en ? reg_gp_1_reg_int_out : 4'bz;  // Controlled_Buffer controlled_buffer_1
endmodule

module rc (
  input  clk,
  input  ring_reset,
  output T1,
  output T2,
  output T3,
  output T4,
  output T5,
  output T6
);

  wire controlled_buffer_1_out, not_1_out;
  wire [3:0] pc_1_pc_value;
  wire [15:6] dec_4x16_1_dec_out;

  assign controlled_buffer_1_out = ring_reset ? ring_reset : 1'bz;  // Controlled_Buffer controlled_buffer_1
  not not_1 (not_1_out, ring_reset);
  assign controlled_buffer_1_out = not_1_out ? dec_4x16_1_dec_out[6] : 1'bz;  // Controlled_Buffer controlled_buffer_2
  pc pc_1 (
    .pc_en(1'b1), .pc_clk(clk), .pc_reset(controlled_buffer_1_out), .pc_out_en(1'b1), .pc_value(pc_1_pc_value));  // open: pc_out
  dec_4x16 dec_4x16_1 (.dec_sel(pc_1_pc_value), .dec_out({dec_4x16_1_dec_out, T6, T5, T4, T3, T2, T1}));
endmodule

module cs (
  input  clk,
  input  clk_reset,
  input  [3:0] ins_msb,
  input  i1,
  input  debug,
  input  i2,
  output sh_dir,
  output sh_out,
  output sh_rot,
  output ins_reg_in_en,
  output a_in,
  output a_out,
  output b_in,
  output alu_out,
  output sram_wr,
  output hlt,
  output sub_out,
  output jump_en,
  output ins_reg_out_en,
  output mar_in_en,
  output sram_rd,
  output pc_out,
  output pc_en
);

  wire and_1_out, and_4_out, and_5_out, and_6_out, and_7_out, and_8_out, and_10_out, and_12_out, and_14_out,
       and_15_out, and_16_out, and_17_out, and_18_out, and_20_out, and_22_out, and_23_out, and_25_out,
       and_27_out, and_28_out, and_29_out, and_30_out, and_32_out, and_34_out, and_35_out, ins_tab_1_insadd,
       ins_tab_1_inshlt, ins_tab_1_insjump, ins_tab_1_inslda, ins_tab_1_insldb, ins_tab_1_insrol,
       ins_tab_1_insror, ins_tab_1_insshl, ins_tab_1_insshr, ins_tab_1_inssta, ins_tab_1_inssub,
       isShiftRot_out, not_1_out, not_2_out, not_3_out, or_1_out, or_3_out, or_4_out, or_5_out, or_6_out,
       or_7_out, or_9_out, or_10_out, rc_1_t1, rc_1_t2, rc_1_t4, rc_1_t5;

  not not_1 (not_1_out, debug);
  not not_2 (not_2_out, debug);
  not not_3 (not_3_out, i2);
  rc rc_1 (
    .clk(clk), .ring_reset(clk_reset), .T1(rc_1_t1), .T2(rc_1_t2), .T3(pc_en), .T4(rc_1_t4), .T5(rc_1_t5));  // open: T6
  ins_tab ins_tab_1 (
    .ir_msb(ins_msb), .insLDA(ins_tab_1_inslda), .insLDB(ins_tab_1_insldb), .insADD(ins_tab_1_insadd),
    .insSUB(ins_tab_1_inssub), .insSTA(ins_tab_1_inssta), .insJump(ins_tab_1_insjump),
    .insSHL(ins_tab_1_insshl), .insSHR(ins_tab_1_insshr), .insROL(ins_tab_1_insrol),
    .insROR(ins_tab_1_insror), .insHLT(ins_tab_1_inshlt));
  and and_1 (and_1_out, ins_tab_1_insjump, pc_en);
  and and_2 (jump_en, not_3_out, and_1_out, not_2_out);
  and and_3 (pc_out, not_2_out, not_3_out, rc_1_t1);
  and and_4 (and_4_out, ins_tab_1_inslda, rc_1_t4);
  or or_1 (or_1_out, rc_1_t1, and_4_out, and_6_out, and_7_out);
  and and_5 (and_5_out, not_1_out, or_1_out);
  or or_2 (mar_in_en, and_5_out, i1);
  and and_6 (and_6_out, ins_tab_1_insldb, rc_1_t4);
  and and_7 (and_7_out, ins_tab_1_inssta, rc_1_t4);
  and and_8 (and_8_out, rc_1_t5, ins_tab_1_inslda);
  or or_3 (or_3_out, rc_1_t2, and_8_out, and_10_out);
  and and_9 (sram_rd, not_2_out, not_3_out, or_3_out);
  and and_10 (and_10_out, rc_1_t5, ins_tab_1_insldb);
  and and_11 (ins_reg_in_en, not_2_out, not_3_out, rc_1_t2);
  and and_12 (and_12_out, rc_1_t4, ins_tab_1_inslda);
  or or_4 (or_4_out, and_12_out, and_14_out, and_15_out, and_16_out);
  and and_13 (ins_reg_out_en, not_2_out, not_3_out, or_4_out);
  and and_14 (and_14_out, rc_1_t4, ins_tab_1_insldb);
  and and_15 (and_15_out, rc_1_t4, ins_tab_1_inssta);
  and and_16 (and_16_out, pc_en, ins_tab_1_insjump);
  and and_17 (and_17_out, rc_1_t5, ins_tab_1_inslda);
  and and_18 (and_18_out, ins_tab_1_inssub, rc_1_t4);
  or or_5 (or_5_out, and_18_out, and_17_out, and_20_out);
  or or_6 (or_6_out, or_5_out, sh_out);
  and and_19 (a_in, not_2_out, not_3_out, or_6_out);
  and and_20 (and_20_out, rc_1_t4, ins_tab_1_insadd);
  and and_21 (a_out, not_2_out, not_3_out, and_22_out);
  and and_22 (and_22_out, rc_1_t5, ins_tab_1_inssta);
  and and_23 (and_23_out, rc_1_t5, ins_tab_1_insldb);
  and and_24 (b_in, not_2_out, not_3_out, and_23_out);
  and and_25 (and_25_out, ins_tab_1_inssub, rc_1_t4);
  or or_7 (or_7_out, and_25_out, and_28_out);
  and and_26 (alu_out, not_2_out, not_3_out, or_7_out);
  and and_27 (and_27_out, rc_1_t5, ins_tab_1_inssta);
  and and_28 (and_28_out, rc_1_t4, ins_tab_1_insadd);
  and and_29 (and_29_out, not_3_out, and_27_out);
  or or_8 (sram_wr, i2, and_29_out);
  and and_30 (and_30_out, ins_tab_1_inshlt, rc_1_t4);
  and and_31 (hlt, not_2_out, not_3_out, and_30_out);
  and and_32 (and_32_out, ins_tab_1_inssub, rc_1_t4);
  and and_33 (sub_out, not_3_out, not_2_out, and_32_out);
  and and_34 (and_34_out, rc_1_t4, not_1_out);
  or isShiftRot (isShiftRot_out, ins_tab_1_insshl, ins_tab_1_insshr, ins_tab_1_insrol, ins_tab_1_insror);
  and and_35 (and_35_out, and_34_out, not_2_out);
  or or_9 (or_9_out, ins_tab_1_insshr, ins_tab_1_insror);
  or or_10 (or_10_out, ins_tab_1_insrol, ins_tab_1_insror);
  and and_36 (sh_out, and_35_out, isShiftRot_out);
  and and_37 (sh_dir, or_9_out, not_1_out);
  and and_38 (sh_rot, or_10_out, not_1_out);
endmodule

module ins_tab (
  input  [3:0] ir_msb,
  output insLDA,
  output insLDB,
  output insADD,
  output insSUB,
  output insSTA,
  output insJump,
  output insSHL,
  output insSHR,
  output insROL,
  output insROR,
  output insHLT
);

  wire [14:0] dec_4x16_1_dec_out;

  dec_4x16 dec_4x16_1 (
    .dec_sel(ir_msb),
    .dec_out({insHLT, dec_4x16_1_dec_out[14:11], insROR, insROL, insSHR, insSHL, insJump, insSTA, insSUB, insADD, insLDB, insLDA, dec_4x16_1_dec_out[0]}));
endmodule

module ins_loader (
  input  bc_reset,
  input  bc_en,
  input  clk,
  input  debug,
  output [3:0] out_5,
  output i1,
  output i2
);

  wire controlled_buffer_1_out, d_ff_1_q, not_1_out;

  Counter #(.max('hf), .width(4)) counter_1 (
    .clr(bc_reset), .load(1'b0), .up(1'b1), .count(bc_en), .clk(clk), .Q(out_5));  // open: D, carry
  assign controlled_buffer_1_out = debug ? not_1_out : 1'bz;  // Controlled_Buffer controlled_buffer_1
  D_Flip_Flop d_ff_1 (.D(controlled_buffer_1_out), .clk(clk), .Q(d_ff_1_q));  // open: Qn, preset, reset
  not not_1 (not_1_out, d_ff_1_q);
  and and_1 (i1, debug, not_1_out);
  and and_2 (i2, debug, d_ff_1_q);
endmodule

module cs_man (
  input  rc_en,
  input  clk,
  input  clk_reset,
  input  [3:0] ins_msb,
  input  mar_in_en_man,
  input  debug,
  input  sram_wr_mannual,
  output pc_en,
  output mar_in_en,
  output sram_rd,
  output a_in,
  output a_out,
  output b_in,
  output hlt,
  output alu_out,
  output sram_wr,
  output sub_out,
  output pc_out,
  output ins_reg_in_en,
  output ins_reg_out_en
);

  wire and_2_out, and_3_out, and_4_out, and_5_out, and_7_out, and_9_out, and_11_out, and_12_out, and_13_out,
       and_15_out, and_17_out, and_18_out, and_20_out, and_22_out, and_23_out, and_25_out, ins_tab_1_insadd,
       ins_tab_1_insjump, ins_tab_1_inslda, ins_tab_1_insldb, ins_tab_1_inssta, ins_tab_1_inssub, not_1_out,
       not_2_out, or_1_out, or_2_out, or_3_out, or_4_out, rc_1_t1, rc_1_t2, rc_1_t4, rc_1_t5;

  not not_1 (not_1_out, debug);
  not not_2 (not_2_out, debug);
  rc rc_1 (
    .clk(rc_en), .ring_reset(clk), .T1(rc_1_t1), .T2(rc_1_t2), .T3(pc_en), .T4(rc_1_t4), .T5(rc_1_t5));  // open: T6
  ins_tab ins_tab_1 (
    .ir_msb(ins_msb), .insLDA(ins_tab_1_inslda), .insLDB(ins_tab_1_insldb), .insADD(ins_tab_1_insadd),
    .insSUB(ins_tab_1_inssub), .insSTA(ins_tab_1_inssta), .insJump(ins_tab_1_insjump),
    .insSHL(ins_tab_1_insjump));  // open: insSHR, insROL, insROR, insHLT
  and and_1 (pc_out, not_2_out, rc_1_t1);
  and and_2 (and_2_out, ins_tab_1_inslda, rc_1_t4);
  or or_1 (or_1_out, rc_1_t1, and_2_out, and_3_out, and_4_out);
  Multiplexer multiplexer_1 (.in0(mar_in_en_man), .in1(or_1_out), .out(mar_in_en), .sel(not_1_out));
  and and_3 (and_3_out, ins_tab_1_insldb, rc_1_t4);
  and and_4 (and_4_out, ins_tab_1_inssta, rc_1_t4);
  and and_5 (and_5_out, rc_1_t5, ins_tab_1_inslda);
  or or_2 (or_2_out, rc_1_t2, and_5_out, and_7_out);
  and and_6 (sram_rd, not_2_out, or_2_out);
  and and_7 (and_7_out, rc_1_t5, ins_tab_1_insldb);
  and and_8 (ins_reg_in_en, not_2_out, rc_1_t2);
  and and_9 (and_9_out, rc_1_t4, ins_tab_1_inslda);
  or or_3 (or_3_out, and_9_out, and_11_out, and_12_out);
  and and_10 (ins_reg_out_en, not_2_out, or_3_out);
  and and_11 (and_11_out, rc_1_t4, ins_tab_1_insldb);
  and and_12 (and_12_out, rc_1_t4, ins_tab_1_inssta);
  and and_13 (and_13_out, rc_1_t5, ins_tab_1_inslda);
  or or_4 (or_4_out, and_13_out, and_15_out);
  and and_14 (a_in, not_2_out, or_4_out);
  and and_15 (and_15_out, rc_1_t4, ins_tab_1_insadd);
  and and_16 (a_out, not_2_out, and_17_out);
  and and_17 (and_17_out, rc_1_t5, ins_tab_1_inssta);
  and and_18 (and_18_out, rc_1_t5, ins_tab_1_insldb);
  and and_19 (b_in, not_2_out, and_18_out);
  and and_20 (and_20_out, rc_1_t4, ins_tab_1_insadd);
  and and_21 (alu_out, not_2_out, and_20_out);
  and and_22 (and_22_out, rc_1_t5, ins_tab_1_inssta);
  Multiplexer multiplexer_2 (.in0(sram_wr_mannual), .in1(and_22_out), .out(sram_wr), .sel(not_1_out));
  and and_23 (and_23_out, ins_tab_1_insjump, rc_1_t4);
  and and_24 (hlt, not_2_out, and_23_out);
  and and_25 (and_25_out, ins_tab_1_inssub, rc_1_t4);
  and and_26 (sub_out, not_2_out, and_25_out);
endmodule

module pc_loader (
  input  pc_reset,
  input  load_or_count,
  input  pc_en,
  input  clk,
  input  [3:0] data_load,
  input  pc_out_en,
  output [3:0] pc_value,
  output [3:0] pc_out
);

  Counter #(.max('hf), .width(4)) counter_1 (
    .clr(pc_reset), .load(load_or_count), .up(1'b1), .count(pc_en), .clk(clk), .D(data_load), .Q(pc_value));  // open: carry
  assign pc_out = pc_out_en ? pc_value : 4'bz;  // Controlled_Buffer controlled_buffer_1
endmodule
