// Logisim project manual_cs.circ as structural Verilog: 13 circuits, main circuit main
module main (
  input  in_1,
  input  in_2,
  input  in_3,
  input  in_4,
  input  in_5,
  input  in_6,
  input  in_7,
  input  in_8,
  input  [7:0] in_9,
  input  [7:0] in_10,
  input  in_11,
  input  in_12,
  input  in_13,
  input  in_14,
  input  in_15,
  input  in_16,
  input  in_17,
  input  [7:0] in_18,
  input  in_19,
  input  in_20,
  input  in_21,
  input  in_22,
  input  in_23,
  input  in_24,
  input  in_25,
  output [3:0] out_26,
  output [7:0] out_27,
  output [7:0] out_28,
  output [7:0] out_29,
  output [7:0] out_30,
  output [7:0] out_31,
  output [7:0] out_32,
  output [7:0] out_33,
  output [7:0] out_34,
  output [7:0] out_35,
  output [7:0] out_36,
  output [7:0] out_37,
  output [7:0] out_38,
  output [7:0] out_39,
  output [7:0] out_40,
  output [7:0] out_41,
  output [7:0] out_42,
  output [7:0] out_43,
  output [7:0] out_44,
  output [7:0] out_45,
  output [3:0] out_46,
  output [3:0] out_47,
  output [7:0] out_48,
  output [7:0] out_49,
  output [7:0] out_50,
  output [7:0] out_51,
  output [7:0] out_52,
  output [7:0] out_53,
  output [3:0] out_54
);

  wire a_in, a_out, alu_out, b_in, hlt, ins_reg_in_en, ins_reg_out_en, mar_in_en, pc_en, pc_out, sram_rd,
       sram_wr, sub_out;
  wire [7:0] reg_gp_3_reg_int_out, reg_gp_4_reg_int_out;

  pc pc_1 (.pc_en(pc_en), .pc_clk(in_7), .pc_reset(in_6), .pc_out_en(pc_out), .pc_value(out_26), .pc_out(out_37[3:0]));
  sram sram_1 (
    .sram_rd(sram_rd), .sram_wr(sram_wr), .sram_d_in(out_37), .mar_d_in(out_37), .mar_in_en(mar_in_en),
    .sram_clk(in_7), .sram_d_out(out_37), .out_8(out_28), .out_9(out_29), .out_10(out_30), .out_11(out_31),
    .out_12(out_32), .out_13(out_33), .out_14(out_34), .out_15(out_35), .out_16(out_36), .out_17(out_38),
    .out_18(out_39), .out_19(out_41), .out_20(out_42), .out_21(out_43), .out_22(out_44), .out_23(out_45));
  assign out_37 = in_8 ? in_9 : 8'bz;  // Controlled_Buffer controlled_buffer_1
  reg_gp reg_gp_1 (
    .reg_in(out_37), .reg_in_en(a_in), .reg_clk(in_7), .reg_out_in(a_out), .reg_int_out(out_27),
    .reg_out(out_37));
  reg_gp reg_gp_2 (
    .reg_in(out_37), .reg_in_en(b_in), .reg_clk(in_7), .reg_out_in(in_1), .reg_int_out(out_40),
    .reg_out(out_37));
  ins_reg ins_reg_1 (
    .ins_reg_in(out_37), .ins_reg_in_en(ins_reg_in_en), .clk(in_7), .ins_reg_out_en(ins_reg_out_en),
    .add_outs(out_37[3:0]), .ins_out(out_47));
  alu alu_1 (
    .alu_in_1(out_27), .alu_out_en(alu_out), .alu_sub(in_2), .alu_in_2(out_40), .alu_out(out_37));  // open: alu_carry_out
  cs_man cs_man_1 (
    .rc_en(in_3), .clk(in_7), .clk_reset(in_6), .ins_msb(out_47), .mar_in_en_man(in_4), .debug(in_8),
    .sram_wr_mannual(in_5), .pc_en(pc_en), .mar_in_en(mar_in_en), .sram_rd(sram_rd), .a_in(a_in),
    .a_out(a_out), .b_in(b_in), .hlt(hlt), .alu_out(alu_out), .sram_wr(sram_wr), .sub_out(sub_out),
    .pc_out(pc_out), .ins_reg_in_en(ins_reg_in_en), .ins_reg_out_en(ins_reg_out_en));
  reg_gp reg_gp_3 (
    .reg_in(in_10), .reg_in_en(in_11), .reg_clk(in_12), .reg_out_in(in_13),
    .reg_int_out(reg_gp_3_reg_int_out), .reg_out(out_49));
  reg_gp reg_gp_4 (
    .reg_in(in_10), .reg_in_en(in_16), .reg_clk(in_12), .reg_out_in(in_17),
    .reg_int_out(reg_gp_4_reg_int_out), .reg_out(out_51));
  alu alu_2 (
    .alu_in_1(reg_gp_3_reg_int_out), .alu_out_en(in_14), .alu_sub(in_15), .alu_in_2(reg_gp_4_reg_int_out),
    .alu_out(out_50));  // open: alu_carry_out
  pc pc_2 (.pc_en(in_22), .pc_clk(in_23), .pc_reset(in_24), .pc_out_en(in_25), .pc_value(out_54));  // open: pc_out
  reg_gp reg_gp_5 (
    .reg_in(in_18), .reg_in_en(in_19), .reg_clk(in_20), .reg_out_in(in_21), .reg_int_out(out_52),
    .reg_out(out_53));

  assign out_46 = out_37[3:0];
  assign out_48 = out_37;

  // Other names for the same wires on the sheet: alu_sub = in_2; b_out = in_1; clk = in_7; cs_en = in_3; debug = in_8;
  //   debug_data[7:0] = in_9; mar_in_en_man = in_4; pc_reset = in_6; sram_wr_man = in_5
endmodule

module reg_gp (
  input  [7:0] reg_in,
  input  reg_in_en,
  input  reg_clk,
  input  reg_out_in,
  output [7:0] reg_int_out,
  output [7:0] reg_out
);

  wire multiplexer_1_out, multiplexer_2_out, multiplexer_3_out, multiplexer_4_out, multiplexer_5_out,
       multiplexer_6_out, multiplexer_7_out, multiplexer_8_out;

  Multiplexer multiplexer_1 (.in0(reg_int_out[7]), .in1(reg_in[7]), .out(multiplexer_1_out), .sel(reg_in_en));
  D_Flip_Flop d_ff_1 (.D(multiplexer_1_out), .clk(reg_clk), .Q(reg_int_out[7]));  // open: Qn, preset, reset
  assign reg_out[7] = reg_out_in ? reg_int_out[7] : 1'bz;  // Controlled_Buffer controlled_buffer_1
  Multiplexer multiplexer_2 (.in0(reg_int_out[6]), .in1(reg_in[6]), .out(multiplexer_2_out), .sel(reg_in_en));
  D_Flip_Flop d_ff_2 (.D(multiplexer_2_out), .clk(reg_clk), .Q(reg_int_out[6]));  // open: Qn, preset, reset
  assign reg_out[6] = reg_out_in ? reg_int_out[6] : 1'bz;  // Controlled_Buffer controlled_buffer_2
  Multiplexer multiplexer_3 (.in0(reg_int_out[5]), .in1(reg_in[5]), .out(multiplexer_3_out), .sel(reg_in_en));
  D_Flip_Flop d_ff_3 (.D(multiplexer_3_out), .clk(reg_clk), .Q(reg_int_out[5]));  // open: Qn, preset, reset
  assign reg_out[5] = reg_out_in ? reg_int_out[5] : 1'bz;  // Controlled_Buffer controlled_buffer_3
  Multiplexer multiplexer_4 (.in0(reg_int_out[4]), .in1(reg_in[4]), .out(multiplexer_4_out), .sel(reg_in_en));
  D_Flip_Flop d_ff_4 (.D(multiplexer_4_out), .clk(reg_clk), .Q(reg_int_out[4]));  // open: Qn, preset, reset
  assign reg_out[4] = reg_out_in ? reg_int_out[4] : 1'bz;  // Controlled_Buffer controlled_buffer_4
  Multiplexer multiplexer_5 (.in0(reg_int_out[3]), .in1(reg_in[3]), .out(multiplexer_5_out), .sel(reg_in_en));
  D_Flip_Flop d_ff_5 (.D(multiplexer_5_out), .clk(reg_clk), .Q(reg_int_out[3]));  // open: Qn, preset, reset
  Multiplexer multiplexer_6 (.in0(reg_int_out[2]), .in1(reg_in[2]), .out(multiplexer_6_out), .sel(reg_in_en));
  D_Flip_Flop d_ff_6 (.D(multiplexer_6_out), .clk(reg_clk), .Q(reg_int_out[2]));  // open: Qn, preset, reset
  assign reg_out[3] = reg_out_in ? reg_int_out[3] : 1'bz;  // Controlled_Buffer controlled_buffer_5
  assign reg_out[2] = reg_out_in ? reg_int_out[2] : 1'bz;  // Controlled_Buffer controlled_buffer_6
  Multiplexer multiplexer_7 (.in0(reg_int_out[1]), .in1(reg_in[1]), .out(multiplexer_7_out), .sel(reg_in_en));
  D_Flip_Flop d_ff_7 (.D(multiplexer_7_out), .clk(reg_clk), .Q(reg_int_out[1]));  // open: Qn, preset, reset
  assign reg_out[1] = reg_out_in ? reg_int_out[1] : 1'bz;  // Controlled_Buffer controlled_buffer_7
  Multiplexer multiplexer_8 (.in0(reg_int_out[0]), .in1(reg_in[0]), .out(multiplexer_8_out), .sel(reg_in_en));
  D_Flip_Flop d_ff_8 (.D(multiplexer_8_out), .clk(reg_clk), .Q(reg_int_out[0]));  // open: Qn, preset, reset
  assign reg_out[0] = reg_out_in ? reg_int_out[0] : 1'bz;  // Controlled_Buffer controlled_buffer_8
endmodule

module alu (
  input  [7:0] alu_in_1,
  input  alu_out_en,
  input  alu_sub,
  input  [7:0] alu_in_2,
  output alu_carry_out,
  output [7:0] alu_out
);

  wire adder_2_cout, adder_3_cout, adder_4_cout, adder_5_cout, adder_6_cout, adder_7_cout, adder_8_cout,
       xor_1_out, xor_2_out, xor_3_out, xor_4_out, xor_5_out, xor_6_out, xor_7_out, xor_8_out;
  wire [7:0] adder_8_out;

  Adder #(.width(1)) adder_1 (
    .a(alu_in_1[7]), .b(xor_1_out), .out(adder_8_out[7]), .cin(adder_2_cout), .cout(alu_carry_out));
  xor xor_1 (xor_1_out, alu_in_2[7], alu_sub);
  Adder #(.width(1)) adder_2 (
    .a(alu_in_1[6]), .b(xor_2_out), .out(adder_8_out[6]), .cin(adder_3_cout), .cout(adder_2_cout));
  xor xor_2 (xor_2_out, alu_in_2[6], alu_sub);
  Adder #(.width(1)) adder_3 (
    .a(alu_in_1[5]), .b(xor_3_out), .out(adder_8_out[5]), .cin(adder_4_cout), .cout(adder_3_cout));
  xor xor_3 (xor_3_out, alu_in_2[5], alu_sub);
  Adder #(.width(1)) adder_4 (
    .a(alu_in_1[4]), .b(xor_4_out), .out(adder_8_out[4]), .cin(adder_5_cout), .cout(adder_4_cout));
  xor xor_4 (xor_4_out, alu_in_2[4], alu_sub);
  Adder #(.width(1)) adder_5 (
    .a(alu_in_1[3]), .b(xor_5_out), .out(adder_8_out[3]), .cin(adder_6_cout), .cout(adder_5_cout));
  xor xor_5 (xor_5_out, alu_in_2[3], alu_sub);
  Adder #(.width(1)) adder_6 (
    .a(alu_in_1[2]), .b(xor_6_out), .out(adder_8_out[2]), .cin(adder_7_cout), .cout(adder_6_cout));
  xor xor_6 (xor_6_out, alu_in_2[2], alu_sub);
  Adder #(.width(1)) adder_7 (
    .a(alu_in_1[1]), .b(xor_7_out), .out(adder_8_out[1]), .cin(adder_8_cout), .cout(adder_7_cout));
  xor xor_7 (xor_7_out, alu_in_2[1], alu_sub);
  Adder #(.width(1)) adder_8 (.a(alu_in_1[0]), .b(xor_8_out), .out(adder_8_out[0]), .cin(alu_sub), .cout(adder_8_cout));
  xor xor_8 (xor_8_out, alu_in_2[0], alu_sub);
  assign alu_out = alu_out_en ? adder_8_out : 8'bz;  // Controlled_Buffer controlled_buffer_1
endmodule

module pc (
  input  pc_en,
  input  pc_clk,
  input  pc_reset,
  input  pc_out_en,
  output [3:0] pc_value,
  output [3:0] pc_out
);

  wire j_k_ff_2_qn, j_k_ff_3_qn, j_k_ff_4_qn;

  J_K_Flip_Flop j_k_ff_1 (
    .J(pc_en), .K(pc_en), .clk(j_k_ff_2_qn), .Q(pc_value[3]), .reset(pc_reset));  // open: Qn, preset
  J_K_Flip_Flop j_k_ff_2 (
    .J(pc_en), .K(pc_en), .clk(j_k_ff_3_qn), .Q(pc_value[2]), .Qn(j_k_ff_2_qn), .reset(pc_reset));  // open: preset
  J_K_Flip_Flop j_k_ff_3 (
    .J(pc_en), .K(pc_en), .clk(j_k_ff_4_qn), .Q(pc_value[1]), .Qn(j_k_ff_3_qn), .reset(pc_reset));  // open: preset
  J_K_Flip_Flop j_k_ff_4 (
    .J(pc_en), .K(pc_en), .clk(pc_clk), .Q(pc_value[0]), .Qn(j_k_ff_4_qn), .reset(pc_reset));  // open: preset
  assign pc_out = pc_out_en ? pc_value : 4'bz;  // Controlled_Buffer controlled_buffer_1
endmodule

module dec_4x16 (
  input  [3:0] dec_sel,
  output [15:0] dec_out
);

  wire not_1_out, not_2_out, not_3_out, not_4_out;

  not not_1 (not_1_out, dec_sel[3]);
  not not_2 (not_2_out, dec_sel[2]);
  not not_3 (not_3_out, dec_sel[1]);
  not not_4 (not_4_out, dec_sel[0]);
  and and_1 (dec_out[0], not_4_out, not_3_out, not_2_out, not_1_out);
  and and_2 (dec_out[1], dec_sel[0], not_3_out, not_2_out, not_1_out);
  and and_3 (dec_out[2], not_4_out, dec_sel[1], not_2_out, not_1_out);
  and and_4 (dec_out[3], dec_sel[0], dec_sel[1], not_2_out, not_1_out);
  and and_5 (dec_out[4], not_4_out, not_3_out, dec_sel[2], not_1_out);
  and and_6 (dec_out[5], dec_sel[0], not_3_out, dec_sel[2], not_1_out);
  and and_7 (dec_out[6], not_4_out, dec_sel[1], dec_sel[2], not_1_out);
  and and_8 (dec_out[7], dec_sel[0], dec_sel[1], dec_sel[2], not_1_out);
  and and_9 (dec_out[8], not_4_out, not_3_out, not_2_out, dec_sel[3]);
  and and_10 (dec_out[9], dec_sel[0], not_3_out, not_2_out, dec_sel[3]);
  and and_11 (dec_out[10], not_4_out, dec_sel[1], not_2_out, dec_sel[3]);
  and and_12 (dec_out[11], dec_sel[0], dec_sel[1], not_2_out, dec_sel[3]);
  and and_13 (dec_out[12], not_4_out, not_3_out, dec_sel[2], dec_sel[3]);
  and and_14 (dec_out[13], dec_sel[0], not_3_out, dec_sel[2], dec_sel[3]);
  and and_15 (dec_out[14], not_4_out, dec_sel[1], dec_sel[2], dec_sel[3]);
  and and_16 (dec_out[15], dec_sel[0], dec_sel[1], dec_sel[2], dec_sel[3]);
endmodule

module sram_cell (
  input  [7:0] data_in,
  input  wr_en,
  input  clk,
  input  cs,
  input  rd_en,
  output [7:0] memory_content,
  output [7:0] data_out
);

  wire and_1_out, and_2_out;

  and and_1 (and_1_out, wr_en, cs);
  and and_2 (and_2_out, cs, rd_en);
  reg_gp reg_gp_1 (
    .reg_in(data_in), .reg_in_en(and_1_out), .reg_clk(clk), .reg_out_in(and_2_out),
    .reg_int_out(memory_content), .reg_out(data_out));
endmodule

module sram (
  input  sram_rd,
  input  sram_wr,
  input  [7:0] sram_d_in,
  input  [7:0] mar_d_in,
  input  mar_in_en,
  input  sram_clk,
  output [7:0] sram_d_out,
  output [7:0] out_8,
  output [7:0] out_9,
  output [7:0] out_10,
  output [7:0] out_11,
  output [7:0] out_12,
  output [7:0] out_13,
  output [7:0] out_14,
  output [7:0] out_15,
  output [7:0] out_16,
  output [7:0] out_17,
  output [7:0] out_18,
  output [7:0] out_19,
  output [7:0] out_20,
  output [7:0] out_21,
  output [7:0] out_22,
  output [7:0] out_23
);

  wire [7:0] controlled_buffer_1_out, reg_gp_1_reg_int_out;
  wire [15:0] dec_4x16_1_dec_out;

  reg_gp reg_gp_1 (
    .reg_in(mar_d_in), .reg_in_en(mar_in_en), .reg_clk(sram_clk), .reg_int_out(reg_gp_1_reg_int_out));  // open: reg_out_in, reg_out
  dec_4x16 dec_4x16_1 (.dec_sel(reg_gp_1_reg_int_out[3:0]), .dec_out(dec_4x16_1_dec_out));
  assign controlled_buffer_1_out = sram_wr ? sram_d_in : 8'bz;  // Controlled_Buffer controlled_buffer_1
  sram_cell sram_cell_1 (
    .data_in(controlled_buffer_1_out), .wr_en(sram_wr), .clk(sram_clk), .cs(dec_4x16_1_dec_out[0]),
    .rd_en(sram_rd), .memory_content(out_8), .data_out(controlled_buffer_1_out));
  sram_cell sram_cell_2 (
    .data_in(controlled_buffer_1_out), .wr_en(sram_wr), .clk(sram_clk), .cs(dec_4x16_1_dec_out[1]),
    .rd_en(sram_rd), .memory_content(out_9), .data_out(controlled_buffer_1_out));
  sram_cell sram_cell_3 (
    .data_in(controlled_buffer_1_out), .wr_en(sram_wr), .clk(sram_clk), .cs(dec_4x16_1_dec_out[2]),
    .rd_en(sram_rd), .memory_content(out_10), .data_out(controlled_buffer_1_out));
  sram_cell sram_cell_4 (
    .data_in(controlled_buffer_1_out), .wr_en(sram_wr), .clk(sram_clk), .cs(dec_4x16_1_dec_out[3]),
    .rd_en(sram_rd), .memory_content(out_11), .data_out(controlled_buffer_1_out));
  sram_cell sram_cell_5 (
    .data_in(controlled_buffer_1_out), .wr_en(sram_wr), .clk(sram_clk), .cs(dec_4x16_1_dec_out[4]),
    .rd_en(sram_rd), .memory_content(out_12), .data_out(controlled_buffer_1_out));
  sram_cell sram_cell_6 (
    .data_in(controlled_buffer_1_out), .wr_en(sram_wr), .clk(sram_clk), .cs(dec_4x16_1_dec_out[5]),
    .rd_en(sram_rd), .memory_content(out_13), .data_out(controlled_buffer_1_out));
  sram_cell sram_cell_7 (
    .data_in(controlled_buffer_1_out), .wr_en(sram_wr), .clk(sram_clk), .cs(dec_4x16_1_dec_out[6]),
    .rd_en(sram_rd), .memory_content(out_14), .data_out(controlled_buffer_1_out));
  sram_cell sram_cell_8 (
    .data_in(controlled_buffer_1_out), .wr_en(sram_wr), .clk(sram_clk), .cs(dec_4x16_1_dec_out[7]),
    .rd_en(sram_rd), .memory_content(out_15), .data_out(controlled_buffer_1_out));
  sram_cell sram_cell_9 (
    .data_in(controlled_buffer_1_out), .wr_en(sram_wr), .clk(sram_clk), .cs(dec_4x16_1_dec_out[8]),
    .rd_en(sram_rd), .memory_content(out_16), .data_out(controlled_buffer_1_out));
  sram_cell sram_cell_10 (
    .data_in(controlled_buffer_1_out), .wr_en(sram_wr), .clk(sram_clk), .cs(dec_4x16_1_dec_out[9]),
    .rd_en(sram_rd), .memory_content(out_17), .data_out(controlled_buffer_1_out));
  sram_cell sram_cell_11 (
    .data_in(controlled_buffer_1_out), .wr_en(sram_wr), .clk(sram_clk), .cs(dec_4x16_1_dec_out[10]),
    .rd_en(sram_rd), .memory_content(out_18), .data_out(controlled_buffer_1_out));
  sram_cell sram_cell_12 (
    .data_in(controlled_buffer_1_out), .wr_en(sram_wr), .clk(sram_clk), .cs(dec_4x16_1_dec_out[11]),
    .rd_en(sram_rd), .memory_content(out_19), .data_out(controlled_buffer_1_out));
  sram_cell sram_cell_13 (
    .data_in(controlled_buffer_1_out), .wr_en(sram_wr), .clk(sram_clk), .cs(dec_4x16_1_dec_out[12]),
    .rd_en(sram_rd), .memory_content(out_20), .data_out(controlled_buffer_1_out));
  sram_cell sram_cell_14 (
    .data_in(controlled_buffer_1_out), .wr_en(sram_wr), .clk(sram_clk), .cs(dec_4x16_1_dec_out[13]),
    .rd_en(sram_rd), .memory_content(out_21), .data_out(controlled_buffer_1_out));
  sram_cell sram_cell_15 (
    .data_in(controlled_buffer_1_out), .wr_en(sram_wr), .clk(sram_clk), .cs(dec_4x16_1_dec_out[14]),
    .rd_en(sram_rd), .memory_content(out_22), .data_out(controlled_buffer_1_out));
  sram_cell sram_cell_16 (
    .data_in(controlled_buffer_1_out), .wr_en(sram_wr), .clk(sram_clk), .cs(dec_4x16_1_dec_out[15]),
    .rd_en(sram_rd), .memory_content(out_23), .data_out(controlled_buffer_1_out));
  assign sram_d_out = sram_rd ? controlled_buffer_1_out : 8'bz;  // Controlled_Buffer controlled_buffer_2
endmodule

module ins_reg (
  input  [7:0] ins_reg_in,
  input  ins_reg_in_en,
  input  clk,
  input  ins_reg_out_en,
  output [3:0] add_outs,
  output [3:0] ins_out
);

  wire [3:0] reg_gp_1_reg_int_out;

  reg_gp reg_gp_1 (
    .reg_in(ins_reg_in), .reg_in_en(ins_reg_in_en), .reg_clk(clk),
    .reg_int_out({ins_out, reg_gp_1_reg_int_out}));  // open: reg_out_in, reg_out
  assign add_outs = ins_reg_out_en ? reg_gp_1_reg_int_out : 4'bz;  // Controlled_Buffer controlled_buffer_1
endmodule

module rc (
  input  rc_en,
  input  clk,
  input  ring_reset,
  output T1,
  output T2,
  output T3,
  output T4,
  output T5,
  output T6
);

  wire controlled_buffer_1_out, not_1_out;
  wire [3:0] pc_1_pc_value;
  wire [15:6] dec_4x16_1_dec_out;

  assign controlled_buffer_1_out = ring_reset ? ring_reset : 1'bz;  // Controlled_Buffer controlled_buffer_1
  not not_1 (not_1_out, ring_reset);
  assign controlled_buffer_1_out = not_1_out ? dec_4x16_1_dec_out[6] : 1'bz;  // Controlled_Buffer controlled_buffer_2
  pc pc_1 (
    .pc_en(rc_en), .pc_clk(clk), .pc_reset(controlled_buffer_1_out), .pc_out_en(rc_en),
    .pc_value(pc_1_pc_value));  // open: pc_out
  dec_4x16 dec_4x16_1 (.dec_sel(pc_1_pc_value), .dec_out({dec_4x16_1_dec_out, T6, T5, T4, T3, T2, T1}));
endmodule

module cs (
  input  rc_en,
  input  clk,
  input  pc_reset,
  input  [3:0] ins_msb,
  input  i1,
  input  debug,
  input  i2,
  output pc_en,
  output mar_in_en,
  output sram_rd,
  output a_in,
  output a_out,
  output b_in,
  output sram_wr,
  output hlt,
  output alu_out,
  output sub_out,
  output pc_out,
  output ins_reg_in_en,
  output ins_reg_out_en
);

  wire and_2_out, and_3_out, and_4_out, and_5_out, and_6_out, and_8_out, and_10_out, and_12_out, and_13_out,
       and_14_out, and_16_out, and_18_out, and_19_out, and_21_out, and_23_out, and_24_out, and_25_out,
       and_27_out, ins_tab_1_insadd, ins_tab_1_inshlt, ins_tab_1_inslda, ins_tab_1_insldb, ins_tab_1_inssta,
       ins_tab_1_inssub, not_1_out, not_2_out, not_3_out, or_1_out, or_3_out, or_4_out, or_5_out, rc_1_t1,
       rc_1_t2, rc_1_t4, rc_1_t5;

  not not_1 (not_1_out, debug);
  not not_2 (not_2_out, debug);
  not not_3 (not_3_out, i2);
  rc rc_1 (
    .rc_en(rc_en), .clk(clk), .ring_reset(pc_reset), .T1(rc_1_t1), .T2(rc_1_t2), .T3(pc_en), .T4(rc_1_t4),
    .T5(rc_1_t5));  // open: T6
  ins_tab ins_tab_1 (
    .ir_msb(ins_msb), .insLDA(ins_tab_1_inslda), .insLDB(ins_tab_1_insldb), .insADD(ins_tab_1_insadd),
    .insSUB(ins_tab_1_inssub), .insSTA(ins_tab_1_inssta), .insHLT(ins_tab_1_inshlt));
  and and_1 (pc_out, not_2_out, not_3_out, rc_1_t1);
  and and_2 (and_2_out, ins_tab_1_inslda, rc_1_t4);
  or or_1 (or_1_out, rc_1_t1, and_2_out, and_4_out, and_5_out);
  and and_3 (and_3_out, not_1_out, or_1_out);
  or or_2 (mar_in_en, and_3_out, i1);
  and and_4 (and_4_out, ins_tab_1_insldb, rc_1_t4);
  and and_5 (and_5_out, ins_tab_1_inssta, rc_1_t4);
  and and_6 (and_6_out, rc_1_t5, ins_tab_1_inslda);
  or or_3 (or_3_out, rc_1_t2, and_6_out, and_8_out);
  and and_7 (sram_rd, not_2_out, not_3_out, or_3_out);
  and and_8 (and_8_out, rc_1_t5, ins_tab_1_insldb);
  and and_9 (ins_reg_in_en, not_2_out, not_3_out, rc_1_t2);
  and and_10 (and_10_out, rc_1_t4, ins_tab_1_inslda);
  or or_4 (or_4_out, and_10_out, and_12_out, and_13_out);
  and and_11 (ins_reg_out_en, not_2_out, not_3_out, or_4_out);
  and and_12 (and_12_out, rc_1_t4, ins_tab_1_insldb);
  and and_13 (and_13_out, rc_1_t4, ins_tab_1_inssta);
  and and_14 (and_14_out, rc_1_t5, ins_tab_1_inslda);
  or or_5 (or_5_out, and_14_out, and_16_out);
  and and_15 (a_in, not_2_out, not_3_out, or_5_out);
  and and_16 (and_16_out, rc_1_t4, ins_tab_1_insadd);
  and and_17 (a_out, not_2_out, not_3_out, and_18_out);
  and and_18 (and_18_out, rc_1_t5, ins_tab_1_inssta);
  and and_19 (and_19_out, rc_1_t5, ins_tab_1_insldb);
  and and_20 (b_in, not_2_out, not_3_out, and_19_out);
  and and_21 (and_21_out, rc_1_t4, ins_tab_1_insadd);
  and and_22 (alu_out, not_2_out, not_3_out, and_21_out);
  and and_23 (and_23_out, rc_1_t5, ins_tab_1_inssta);
  and and_24 (and_24_out, not_3_out, and_23_out);
  or or_6 (sram_wr, i2, and_24_out);
  and and_25 (and_25_out, ins_tab_1_inshlt, rc_1_t4);
  and and_26 (hlt, not_2_out, not_3_out, and_25_out);
  and and_27 (and_27_out, ins_tab_1_inssub, rc_1_t4);
  and and_28 (sub_out, not_2_out, and_27_out);
endmodule

module ins_tab (
  input  [3:0] ir_msb,
  output insLDA,
  output insLDB,
  output insADD,
  output insSUB,
  output insSTA,
  output insHLT
);

  wire [15:0] dec_4x16_1_dec_out;

  dec_4x16 dec_4x16_1 (
    .dec_sel(ir_msb),
    .dec_out({dec_4x16_1_dec_out[15], insHLT, dec_4x16_1_dec_out[13:6], insSTA, insSUB, insADD, insLDB, insLDA, dec_4x16_1_dec_out[0]}));
endmodule

module ins_loader (
  input  bc_reset,
  input  bc_en,
  input  clk,
  input  debug,
  output [3:0] out_5,
  output i1,
  output i2
);

  wire controlled_buffer_1_out, d_ff_1_q, not_1_out;

  Counter #(.max('hf), .width(4)) counter_1 (
    .clr(bc_reset), .load(1'b0), .up(1'b1), .count(bc_en), .clk(clk), .Q(out_5));  // open: D, carry
  assign controlled_buffer_1_out = debug ? not_1_out : 1'bz;  // Controlled_Buffer controlled_buffer_1
  D_Flip_Flop d_ff_1 (.D(controlled_buffer_1_out), .clk(clk), .Q(d_ff_1_q));  // open: Qn, preset, reset
  not not_1 (not_1_out, d_ff_1_q);
  and and_1 (i1, debug, not_1_out);
  and and_2 (i2, debug, d_ff_1_q);
endmodule

module cs_man (
  input  rc_en,
  input  clk,
  input  clk_reset,
  input  [3:0] ins_msb,
  input  mar_in_en_man,
  input  debug,
  input  sram_wr_mannual,
  output pc_en,
  output mar_in_en,
  output sram_rd,
  output a_in,
  output a_out,
  output b_in,
  output hlt,
  output alu_out,
  output sram_wr,
  output sub_out,
  output pc_out,
  output ins_reg_in_en,
  output ins_reg_out_en
);

  wire and_2_out, and_3_out, and_4_out, and_5_out, and_7_out, and_9_out, and_11_out, and_12_out, and_13_out,
       and_15_out, and_17_out, and_18_out, and_20_out, and_22_out, and_23_out, and_25_out, ins_tab_1_p2,
       ins_tab_1_p3, ins_tab_1_p4, ins_tab_1_p5, ins_tab_1_p6, ins_tab_1_p7, not_1_out, not_2_out, or_1_out,
       or_2_out, or_3_out, or_4_out, rc_1_t1, rc_1_t2, rc_1_t4, rc_1_t5;

  not not_1 (not_1_out, debug);
  not not_2 (not_2_out, debug);
  rc rc_1 (
    .rc_en(rc_en), .clk(clk), .ring_reset(clk_reset), .T1(rc_1_t1), .T2(rc_1_t2), .T3(pc_en), .T4(rc_1_t4),
    .T5(rc_1_t5));  // open: T6
  // ins_tab ins_tab_1: pin names not known; wires that end beside it: ins_msb, ins_tab_1_p2, ins_tab_1_p3, ins_tab_1_p4, ins_tab_1_p5, ins_tab_1_p6, ins_tab_1_p7
  and and_1 (pc_out, not_2_out, rc_1_t1);
  and and_2 (and_2_out, ins_tab_1_p2, rc_1_t4);
  or or_1 (or_1_out, rc_1_t1, and_2_out, and_3_out, and_4_out);
  Multiplexer multiplexer_1 (.in0(mar_in_en_man), .in1(or_1_out), .out(mar_in_en), .sel(not_1_out));
  and and_3 (and_3_out, ins_tab_1_p3, rc_1_t4);
  and and_4 (and_4_out, ins_tab_1_p6, rc_1_t4);
  and and_5 (and_5_out, rc_1_t5, ins_tab_1_p2);
  or or_2 (or_2_out, rc_1_t2, and_5_out, and_7_out);
  and and_6 (sram_rd, not_2_out, or_2_out);
  and and_7 (and_7_out, rc_1_t5, ins_tab_1_p3);
  and and_8 (ins_reg_in_en, not_2_out, rc_1_t2);
  and and_9 (and_9_out, rc_1_t4, ins_tab_1_p2);
  or or_3 (or_3_out, and_9_out, and_11_out, and_12_out);
  and and_10 (ins_reg_out_en, not_2_out, or_3_out);
  and and_11 (and_11_out, rc_1_t4, ins_tab_1_p3);
  and and_12 (and_12_out, rc_1_t4, ins_tab_1_p6);
  and and_13 (and_13_out, rc_1_t5, ins_tab_1_p2);
  or or_4 (or_4_out, and_13_out, and_15_out);
  and and_14 (a_in, not_2_out, or_4_out);
  and and_15 (and_15_out, rc_1_t4, ins_tab_1_p4);
  and and_16 (a_out, not_2_out, and_17_out);
  and and_17 (and_17_out, rc_1_t5, ins_tab_1_p6);
  and and_18 (and_18_out, rc_1_t5, ins_tab_1_p3);
  and and_19 (b_in, not_2_out, and_18_out);
  and and_20 (and_20_out, rc_1_t4, ins_tab_1_p4);
  and and_21 (alu_out, not_2_out, and_20_out);
  and and_22 (and_22_out, rc_1_t5, ins_tab_1_p6);
  Multiplexer multiplexer_2 (.in0(sram_wr_mannual), .in1(and_22_out), .out(sram_wr), .sel(not_1_out));
  and and_23 (and_23_out, ins_tab_1_p7, rc_1_t4);
  and and_24 (hlt, not_2_out, and_23_out);
  and and_25 (and_25_out, ins_tab_1_p5, rc_1_t4);
  and and_26 (sub_out, not_2_out, and_25_out);
endmodule
